// Logisim project GatePulseSequencer_Project.circ as structural Verilog: 1 circuit, main circuit main
module main (
);

  wire CLK_out, comparator_1_eq, DFF_0A_q, DFF_0B_q, DFF_0C_q, DFF_1A_q, DFF_1B_q, DFF_1C_q, DFF_2A_q,
       DFF_2B_q, DFF_2C_q, DFF_3A_q, DFF_3B_q, DFF_3C_q, Fault_out, multiplexer_2_out, Not_0A_out,
       Not_1A_out, Not_1B_out, Not_2A_out, Not_2B_out, Not_3A_out, Not_3B_out;
  wire [3:0] adder_1_out, Divcnt_q, multiplexer_1_out;

  Button Fault (.out(Fault_out));
  Register #(.width(4)) Divcnt (.D(multiplexer_1_out), .clk(CLK_out), .Q(Divcnt_q));  // open: en, clr
  Clock CLK (.out(CLK_out));
  Comparator #(.mode("unsigned"), .width(4)) comparator_1 (
    .a(Divcnt_q), .b(4'b0011), .eq(comparator_1_eq));  // open: gt, lt
  Adder #(.width(4)) adder_1 (.a(Divcnt_q), .b(4'b0001), .out(adder_1_out));  // open: cin, cout
  Multiplexer #(.width(4)) multiplexer_1 (
    .in0(adder_1_out), .in1(4'b0000), .out(multiplexer_1_out), .sel(comparator_1_eq));
  D_Flip_Flop DFF_0A (.D(DFF_3A_q), .clk(comparator_1_eq), .Q(DFF_0A_q));  // open: Qn, preset, reset
  D_Flip_Flop DFF_1A (.D(DFF_0A_q), .clk(comparator_1_eq), .Q(DFF_1A_q));  // open: Qn, preset, reset
  D_Flip_Flop DFF_2A (.D(DFF_1A_q), .clk(comparator_1_eq), .Q(DFF_2A_q));  // open: Qn, preset, reset
  D_Flip_Flop DFF_3A (.D(DFF_2A_q), .clk(comparator_1_eq), .Q(DFF_3A_q));  // open: Qn, preset, reset
  not Not_0A (Not_0A_out, DFF_0A_q);
  LED led_1 (.in(Not_0A_out));
  not Not_1A (Not_1A_out, DFF_1A_q);
  LED led_2 (.in(Not_1A_out));
  not Not_2A (Not_2A_out, DFF_2A_q);
  LED led_3 (.in(Not_2A_out));
  not Not_3A (Not_3A_out, DFF_3A_q);
  LED led_4 (.in(Not_3A_out));
  D_Flip_Flop DFF_0B (.D(DFF_0A_q), .clk(comparator_1_eq), .Q(DFF_0B_q));  // open: Qn, preset, reset
  D_Flip_Flop DFF_1B (.D(DFF_1A_q), .clk(comparator_1_eq), .Q(DFF_1B_q));  // open: Qn, preset, reset
  D_Flip_Flop DFF_2B (.D(DFF_2A_q), .clk(comparator_1_eq), .Q(DFF_2B_q));  // open: Qn, preset, reset
  D_Flip_Flop DFF_3B (.D(DFF_3A_q), .clk(comparator_1_eq), .Q(DFF_3B_q));  // open: Qn, preset, reset
  LED U0_final (.in(DFF_0B_q));
  LED U1_final (.in(DFF_1B_q));
  LED U2_final (.in(DFF_2B_q));
  LED U3_final (.in(DFF_3B_q));
  Multiplexer multiplexer_2 (.in0(DFF_0B_q), .in1(1'b0), .out(multiplexer_2_out), .sel(Fault_out));
  // NOT_Gate Not_0B has open pins: in=DFF_0B_q, out=open
  not Not_1B (Not_1B_out, DFF_1B_q);
  not Not_2B (Not_2B_out, DFF_2B_q);
  not Not_3B (Not_3B_out, DFF_3B_q);
  D_Flip_Flop DFF_0C (.D(multiplexer_2_out), .clk(comparator_1_eq), .Q(DFF_0C_q));  // open: Qn, preset, reset
  D_Flip_Flop DFF_1C (.D(Not_1B_out), .clk(comparator_1_eq), .Q(DFF_1C_q));  // open: Qn, preset, reset
  D_Flip_Flop DFF_2C (.D(Not_2B_out), .clk(comparator_1_eq), .Q(DFF_2C_q));  // open: Qn, preset, reset
  D_Flip_Flop DFF_3C (.D(Not_3B_out), .clk(comparator_1_eq), .Q(DFF_3C_q));  // open: Qn, preset, reset
  LED L0_LED (.in(DFF_0C_q));
  LED L1_LED (.in(DFF_1C_q));
  LED L2_LED (.in(DFF_2C_q));
  LED L3_LED (.in(DFF_3C_q));
endmodule
